# Fritzing sketch beer-tc-final (saved by Fritzing 0.9.3b)
breadboards: 1

parts:
  LCD1 = LCD screen
  R2 = Resistor [tolerance=±5% resistance=220 package=THT]
  Q1_-_BS170 = Basic FET N-Channel [package="TO220 [THT]"]
  U1 = RELAY-SOLIDSTATE [package=relay-s108t02]
  AT_Pro_Mini = Arduino Pro Mini (5V)
  R1 = Rotary Potentiometer (Small) [maximum_resistance=10kΩ package=THT]
  R3 = Resistor [tolerance=±5% resistance=10k package=THT]
  R4 = Resistor [tolerance=±5% resistance=4.7k package=THT]
  R5 = Resistor [tolerance=±5% resistance=4.7k package=THT]
  T2 = DS18B20 1-Wire Temperature Sensor [part_number=DS18B20]
  T1 = DS18B20 1-Wire Temperature Sensor [part_number=DS18B20]

nets:
  GND: LCD1.VSS, LCD1.LED-, Q1_-_BS170.source, AT_Pro_Mini.GND, R1.leg2, R3.Pin_1, T2.GND, T1.GND
  5V: LCD1.VDD, R2.Pin_0, U1.+, AT_Pro_Mini.RAW, R1.leg1
  N1: LCD1.V0, R1.wiper
  N2: LCD1.RS, AT_Pro_Mini.D2
  N3: LCD1.R/W, AT_Pro_Mini.D8
  N4: LCD1.E, AT_Pro_Mini.D3
  N5: LCD1.DB4, AT_Pro_Mini.D4
  N6: LCD1.DB5, AT_Pro_Mini.D5
  N7: LCD1.DB6, AT_Pro_Mini.D6
  N8: LCD1.DB7, AT_Pro_Mini.D7
  N9: LCD1.LED+, R2.Pin_1
  N10: Q1_-_BS170.gate, AT_Pro_Mini.D9, R3.Pin_0
  N11: Q1_-_BS170.drain, U1.-
  Serial TX: AT_Pro_Mini.TXO
  3.3V: AT_Pro_Mini.VCC, R4.Pin_0, R5.Pin_0, T2.VDD, T1.VDD
  N12: AT_Pro_Mini.A1, R4.Pin_1, T2.DQ
  N13: AT_Pro_Mini.A0, R5.Pin_1, T1.DQ
  Serial RX: AT_Pro_Mini.RXI

notes:
  To heater/cooler
  3V3 rail, max 150mA
